# Fritzing sketch simulant (saved by Fritzing 0.9.3b)
breadboards: 1

parts:
  U5_-_HC-05 = Bluetooth HC-05 Macho
  U4 = Arduino Nano (Rev3.0) (ICSP)
  BAT1 = 18650 battery holder [package=battery-18650-kit]
  U1 = TP4056 [chip_label=TP4056 package="DIP (Dual Inline) [THT]"]
  S1_-_ON_/OFF_SWITCH = Taiway 100-SP-X-T1 SPDT Miniature Toggle Switch [package=THT]
  R1_1k = PHOTOCELL [package=photocell]
  LED1 = smd LED [color="White (8000K)" package="1206 [SMD]"]
  X2_-_4-20mA_I_IN_+_/_24VDC_+_/_PULSE_+ = BANANA_CONN [package=banana_conn]
  R3 = Rotary Potentiometer (Large) [maximum_resistance=10kΩ package=THT]
  D1 = Diode [package=diode-1n4001]
  Q1 = NPN-Transistor [package="TO92 [THT]"]
  5VDC_IN = Power Jack [package=power_jack_combo]
  R4 = Resistor [tolerance=±5% resistance=1.5k package="0603 [SMD]"]
  R5 = Resistor [tolerance=±5% resistance=1.5k package="0603 [SMD]"]
  J7 = Camdenboss CTB0158-3 [part_number=CTB0158-3 package=THT]
  U3_PWM_-_4-20mA_MODULE = Camdenboss CTB0158-2 [package=THT]
  X3_-_4-20mA_I_OUT_+ = BANANA_CONN [package=banana_conn]
  X3_-_1-20mA_I_OUT_- = BANANA_CONN [package=banana_conn]
  R6 = Resistor [tolerance=±5% resistance=2k package="0603 [SMD]"]
  S2_-_I_IN_/_I_OUT_SWITCH = SPDT Slide Switch [package=ayz0202]
  R7 = Resistor [tolerance=±5% resistance=150 package="0603 [SMD]"]
  X2_4-20mA_I_IN_-_/_24VDC_-_/_PULSE_- = BANANA_CONN [package=banana_conn]
  X1_-_PT100_(1) = BANANA_CONN [package=banana_conn]
  X1_-_PT100_(2) = BANANA_CONN [package=banana_conn]
  R2 = Resistor [tolerance=±5% resistance=150 package="0603 [SMD]"]
  R7_2 = Resistor [tolerance=±5% resistance=50 package="0603 [SMD]"]
  X4_-_PULSE_IN_/_OUT = BANANA_CONN [package=banana_conn]
  R8 = Resistor [tolerance=±5% resistance=5k package="0603 [SMD]"]
  R9 = Resistor [tolerance=±5% resistance=10k package="0603 [SMD]"]
  C1_100n = Capacitor [package=cap-pth-small2]
  U2 = DC-DC 2-24V Step Up Booster [package=THT]
  R10 = Resistor [tolerance=±5% resistance=80k package="0603 [SMD]"]
  R11 = Resistor [tolerance=±5% resistance=10k package="0603 [SMD]"]
  D2 = Diode [package=diode-1n4001]
  D3 = Diode [package=diode-1n4001]
  D4 = Diode [package=diode-1n4001]
  R12 = Resistor [tolerance=±5% resistance=1.5k package="0603 [SMD]"]
  R13 = Resistor [tolerance=±5% resistance=1.5k package="0603 [SMD]"]
  D5 = Zener Diode [part_number=1N4732A breakdown_voltage=3.6V package="Melf DO-213 AB [SMD]"]
  R14 = Resistor [tolerance=±5% resistance=1.5k package="0603 [SMD]"]

nets:
  N1: U5_-_HC-05.TXD, U4.D0/RX
  N2: U5_-_HC-05.RXD, R4.Pin_1, R5.Pin_0
  VCC: U5_-_HC-05.VCC, U4.3V3
  GND: U5_-_HC-05.GND, U4.GND, U1.pin6, LED1.cathode, R3.leg1, Q1.E, R4.Pin_0, J7.pin1, U3_PWM_-_4-20mA_MODULE.pin2, R7.Pin_1, X2_4-20mA_I_IN_-_/_24VDC_-_/_PULSE_-.1, C1_100n.1, U2.pin2, U2.pin4, R11.Pin_0, D4.A, R12.Pin_0, D5.anode
  N3: U4.D1/TX, R5.Pin_1
  N4: U4.D4, R9.Pin_0
  N5: U4.D5, R7_2.Pin_0
  N6: U4.D6, U3_PWM_-_4-20mA_MODULE.pin1
  N7: U4.D8, R10.Pin_0, R11.Pin_1
  N8: U4.5V, R3.leg2, D1.C, R13.Pin_1, R14.Pin_1
  N9: U4.A7, X3_-_1-20mA_I_OUT_-.1, S2_-_I_IN_/_I_OUT_SWITCH.5, R7.Pin_0, C1_100n.2
  N10: U4.A6, R3.wiper
  N11: U4.A5, R12.Pin_1, R13.Pin_0
  N12: U4.AREF, D5.cathode, R14.Pin_0
  N13: BAT1.+, U1.pin4
  N14: BAT1.-, U1.pin5
  N15: U1.pin1, 5VDC_IN.PWR
  N16: U1.pin2, 5VDC_IN.GND
  N17: U1.pin3, S1_-_ON_/OFF_SWITCH.L2
  N18: S1_-_ON_/OFF_SWITCH.COM, D1.A, U2.pin3
  N19: R1_1k.P$1, X1_-_PT100_(1).1, R2.Pin_1
  N20: R1_1k.P$2, X1_-_PT100_(2).1, R2.Pin_0
  N21: LED1.anode, R7_2.Pin_1
  N22: X2_-_4-20mA_I_IN_+_/_24VDC_+_/_PULSE_+.1, J7.pin3, S2_-_I_IN_/_I_OUT_SWITCH.2, R8.Pin_1, D4.C
  N23: Q1.B, R9.Pin_1
  N24: Q1.C, X4_-_PULSE_IN_/_OUT.1, R8.Pin_0, R10.Pin_1
  N25: J7.pin2, R6.Pin_1, D2.A
  N26: X3_-_4-20mA_I_OUT_+.1, D2.C
  N27: R6.Pin_0, S2_-_I_IN_/_I_OUT_SWITCH.6
  N28: S2_-_I_IN_/_I_OUT_SWITCH.1, D3.C
  N29: U2.pin1, D3.A

notes:
  X1 - PT100 (1)
  X1 - PT100 (2)
  X2 - 4-20mA I IN + / 24VDC + / PULSE +
  X2 - 4-20mA I IN - / 24VDC - / PULSE -
  X3 - 4-20mA I OUT +
  X3 - 4-20mA I OUT -
  X4 - PULSE IN /OUT
  5VDC IN
  PWM / 4-20mA
  MODULE
  S2 - I IN / I OUT
  SWITCH
  S1 - ON / OFF SWITCH

custom parts:
  18650 battery holder: 18650 Battery Holder
  TP4056: A DIP stand-in part for whatever IC you want. With 6 pins on a 300mil dual inline package (DIP) footprint.
  DC-DC 2-24V Step Up Booster: Convertisseur DC-DC 2-24V 2A
